// Digital circuit Beyzagul_Demir_Lab2.dig as structural Verilog
module Beyzagul_Demir_Lab2 (
  input  in_1,
  input  in_2,
  input  in_3,
  input  in_4,
  input  in_5
);

  wire _7448_1_pin9, _7448_1_pin10, _7448_1_pin11, _7448_1_pin12, _7448_1_pin13, _7448_1_pin14,
       _7448_1_pin15, a0_out, a1_out, a2_out, add_1_c_o, add_1_s, add_2_c_o, add_2_s, add_3_c_o, add_3_s,
       b0_out, b1_out, b2_out;

  DipSwitch a2 (.out(a2_out));
  DipSwitch b2 (.out(b2_out));
  Add add_1 (.a(b2_out), .b(a2_out), .c_i(add_2_c_o), .s(add_1_s), .c_o(add_1_c_o));
  LED led_1 (.in(add_1_s));
  DipSwitch a1 (.out(a1_out));
  DipSwitch b1 (.out(b1_out));
  Add add_2 (.a(b1_out), .b(a1_out), .c_i(add_3_c_o), .s(add_2_s), .c_o(add_2_c_o));
  DipSwitch a0 (.out(a0_out));
  DipSwitch b0 (.out(b0_out));
  Add add_3 (.a(b0_out), .b(a0_out), .c_i(in_1), .s(add_3_s), .c_o(add_3_c_o));
  _7448 _7448_1 (
    .pin1(add_2_s), .pin2(add_1_s), .pin3(in_3), .pin4(in_4), .pin5(in_5), .pin6(in_2), .pin7(add_3_s),
    .pin8(1'b0), .pin9(_7448_1_pin9), .pin10(_7448_1_pin10), .pin11(_7448_1_pin11), .pin12(_7448_1_pin12),
    .pin13(_7448_1_pin13), .pin14(_7448_1_pin14), .pin15(_7448_1_pin15), .pin16(1'b1));
  Seven_Seg seven_seg_1 (
    .a(_7448_1_pin13), .b(_7448_1_pin12), .c(_7448_1_pin11), .d(_7448_1_pin10), .e(_7448_1_pin9),
    .f(_7448_1_pin15), .g(_7448_1_pin14), .dp(1'b0));
  // also tied to GND on the sheet: add_1_c_o

  // Notes on the sheet:
  //   in_3: default 1
  //   in_4: default 1
  //   in_5: default 1
endmodule
